// Logisim project tmi.circ as structural Verilog: 4 circuits, main circuit cell
module main (
);

  wire cell_1_clk_2, cell_1_is_active_2, cell_1_set_head, cell_2_clk_2, cell_2_is_active, cell_2_is_active_2,
       cell_2_set_head, cell_2_set_tail, cell_3_clk_2, cell_3_is_active, cell_3_is_active_2, cell_3_set_head,
       cell_3_set_tail, cell_4_clk_2, cell_4_is_active, cell_4_is_active_2, cell_4_set_head, cell_4_set_tail,
       cell_5_is_active, cell_5_set_tail, clock_1_out, cpu_1_cell_clk, cpu_1_fake_act, cpu_1_tape_next,
       cpu_1_tape_prev, cpu_1_tty_clk, START_out;
  wire [2:0] cell_1_cmd_2, cell_1_dbg_led, cell_2_cmd_2, cell_2_dbg_led, cell_3_cmd_2, cell_3_dbg_led,
       cell_4_cmd_2, cell_4_dbg_led, cell_5_cmd_2, cell_5_dbg_led, cpu_1_cmd;
  wire [3:0] cell_1_dbg_mem, cell_1_dbg_mem_2, cell_2_dbg_mem, cell_2_dbg_mem_2, cell_3_dbg_mem,
       cell_3_dbg_mem_2, cell_4_dbg_mem, cell_4_dbg_mem_2, cell_5_dbg_mem, cell_5_dbg_mem_2, rom_2_data,
       tape_1_bf_cmd;
  wire [6:0] cpu_1_disp;
  wire [7:0] cell_1_data_in_2, cell_1_data_out_2, cell_2_data_in_2, cell_2_data_out_2, cell_3_data_in_2,
       cell_3_data_out_2, cell_4_data_in_2, cell_4_data_out_2, cell_5_data_out_2, cpu_1_data_to_cell;
  wire [11:0] tape_1_address;

  ROM #(.addrWidth(12), .dataWidth(4)) rom_1 ();  // open: addr, data, sel
  ROM #(.addrWidth(12), .dataWidth(4)) rom_2 (.addr(tape_1_address), .data(rom_2_data));  // open: sel
  tape tape_1 (
    .ADDRESS(tape_1_address), .DATA(rom_2_data), .BF_CMD(tape_1_bf_cmd), .BF_NEXT(cpu_1_tape_next),
    .BF_PREV(cpu_1_tape_prev));
  TTY tty_1 (.data(cpu_1_disp), .clk(cpu_1_tty_clk));  // open: we, clr
  cpu cpu_1 (
    .CUR_BF(tape_1_bf_cmd), .TAPE_NEXT(cpu_1_tape_next), .TAPE_PREV(cpu_1_tape_prev), .DISP(cpu_1_disp),
    .TTY_CLK(cpu_1_tty_clk), .CLK(clock_1_out), .TURN_ON(START_out), .FAKE_ACT(cpu_1_fake_act),
    .DATA_TO_CELL(cpu_1_data_to_cell), .DATA_FROM_CELL(cell_1_data_out_2), .CMD(cpu_1_cmd),
    .CELL_CLK(cpu_1_cell_clk));
  Clock clock_1 (.out(clock_1_out));
  Button START (.out(START_out));
  DotMatrix #(.matrixcols(3), .matrixrows(1)) dotmatrix_1 (
    .col0(cell_1_dbg_led[0]), .col1(cell_1_dbg_led[1]), .col2(cell_1_dbg_led[2]));
  Hex_Digit_Display hex_digit_display_1 (.value(cell_1_dbg_mem_2));  // open: dp
  \cell  cell_1 (
    .IS_ACTIVE_LEFT(cpu_1_fake_act), .DATA_IN(cpu_1_data_to_cell), .DATA_OUT_2(cell_1_data_out_2),
    .CMD(cpu_1_cmd), .CLK(cpu_1_cell_clk), .IS_TAIL(cell_2_set_tail), .SET_HEAD(cell_1_set_head),
    .IS_ACTIVE_RIGHT(cell_2_is_active), .IS_ACTIVE_2(cell_1_is_active_2), .DATA_IN_2(cell_1_data_in_2),
    .DATA_OUT(cell_2_data_out_2), .CMD_2(cell_1_cmd_2), .CLK_2(cell_1_clk_2),
    .DBG_MEM({cell_1_dbg_mem_2, cell_1_dbg_mem}), .DBG_LED(cell_1_dbg_led));  // open: SET_TAIL, IS_HEAD, IS_ACTIVE
  Hex_Digit_Display hex_digit_display_2 (.value(cell_1_dbg_mem));  // open: dp
  \cell  cell_2 (
    .SET_TAIL(cell_2_set_tail), .IS_HEAD(cell_1_set_head), .IS_ACTIVE(cell_2_is_active),
    .IS_ACTIVE_LEFT(cell_1_is_active_2), .DATA_IN(cell_1_data_in_2), .DATA_OUT_2(cell_2_data_out_2),
    .CMD(cell_1_cmd_2), .CLK(cell_1_clk_2), .IS_TAIL(cell_3_set_tail), .SET_HEAD(cell_2_set_head),
    .IS_ACTIVE_RIGHT(cell_3_is_active), .IS_ACTIVE_2(cell_2_is_active_2), .DATA_IN_2(cell_2_data_in_2),
    .DATA_OUT(cell_3_data_out_2), .CMD_2(cell_2_cmd_2), .CLK_2(cell_2_clk_2),
    .DBG_MEM({cell_2_dbg_mem_2, cell_2_dbg_mem}), .DBG_LED(cell_2_dbg_led));
  DotMatrix #(.matrixcols(3), .matrixrows(1)) dotmatrix_2 (
    .col0(cell_2_dbg_led[0]), .col1(cell_2_dbg_led[1]), .col2(cell_2_dbg_led[2]));
  Hex_Digit_Display hex_digit_display_3 (.value(cell_2_dbg_mem_2));  // open: dp
  Hex_Digit_Display hex_digit_display_4 (.value(cell_2_dbg_mem));  // open: dp
  DotMatrix #(.matrixcols(3), .matrixrows(1)) dotmatrix_3 (
    .col0(cell_3_dbg_led[0]), .col1(cell_3_dbg_led[1]), .col2(cell_3_dbg_led[2]));
  Hex_Digit_Display hex_digit_display_5 (.value(cell_3_dbg_mem_2));  // open: dp
  \cell  cell_3 (
    .SET_TAIL(cell_3_set_tail), .IS_HEAD(cell_2_set_head), .IS_ACTIVE(cell_3_is_active),
    .IS_ACTIVE_LEFT(cell_2_is_active_2), .DATA_IN(cell_2_data_in_2), .DATA_OUT_2(cell_3_data_out_2),
    .CMD(cell_2_cmd_2), .CLK(cell_2_clk_2), .IS_TAIL(cell_4_set_tail), .SET_HEAD(cell_3_set_head),
    .IS_ACTIVE_RIGHT(cell_4_is_active), .IS_ACTIVE_2(cell_3_is_active_2), .DATA_IN_2(cell_3_data_in_2),
    .DATA_OUT(cell_4_data_out_2), .CMD_2(cell_3_cmd_2), .CLK_2(cell_3_clk_2),
    .DBG_MEM({cell_3_dbg_mem_2, cell_3_dbg_mem}), .DBG_LED(cell_3_dbg_led));
  Hex_Digit_Display hex_digit_display_6 (.value(cell_3_dbg_mem));  // open: dp
  \cell  cell_4 (
    .SET_TAIL(cell_4_set_tail), .IS_HEAD(cell_3_set_head), .IS_ACTIVE(cell_4_is_active),
    .IS_ACTIVE_LEFT(cell_3_is_active_2), .DATA_IN(cell_3_data_in_2), .DATA_OUT_2(cell_4_data_out_2),
    .CMD(cell_3_cmd_2), .CLK(cell_3_clk_2), .IS_TAIL(cell_5_set_tail), .SET_HEAD(cell_4_set_head),
    .IS_ACTIVE_RIGHT(cell_5_is_active), .IS_ACTIVE_2(cell_4_is_active_2), .DATA_IN_2(cell_4_data_in_2),
    .DATA_OUT(cell_5_data_out_2), .CMD_2(cell_4_cmd_2), .CLK_2(cell_4_clk_2),
    .DBG_MEM({cell_4_dbg_mem_2, cell_4_dbg_mem}), .DBG_LED(cell_4_dbg_led));
  DotMatrix #(.matrixcols(3), .matrixrows(1)) dotmatrix_4 (
    .col0(cell_4_dbg_led[0]), .col1(cell_4_dbg_led[1]), .col2(cell_4_dbg_led[2]));
  Hex_Digit_Display hex_digit_display_7 (.value(cell_4_dbg_mem));  // open: dp
  Hex_Digit_Display hex_digit_display_8 (.value(cell_4_dbg_mem_2));  // open: dp
  DotMatrix #(.matrixcols(3), .matrixrows(1)) dotmatrix_5 (
    .col0(cell_5_dbg_led[0]), .col1(cell_5_dbg_led[1]), .col2(cell_5_dbg_led[2]));
  Hex_Digit_Display hex_digit_display_9 (.value(cell_5_dbg_mem_2));  // open: dp
  \cell  cell_5 (
    .SET_TAIL(cell_5_set_tail), .IS_HEAD(cell_4_set_head), .IS_ACTIVE(cell_5_is_active),
    .IS_ACTIVE_LEFT(cell_4_is_active_2), .DATA_IN(cell_4_data_in_2), .DATA_OUT_2(cell_5_data_out_2),
    .CMD(cell_4_cmd_2), .CLK(cell_4_clk_2), .CMD_2(cell_5_cmd_2),
    .DBG_MEM({cell_5_dbg_mem_2, cell_5_dbg_mem}), .DBG_LED(cell_5_dbg_led));  // open: IS_TAIL, SET_HEAD, IS_ACTIVE_RIGHT, IS_ACTIVE_2, DATA_IN_2, DATA_OUT, CLK_2
  Hex_Digit_Display hex_digit_display_10 (.value(cell_5_dbg_mem));  // open: dp
  Hex_Digit_Display hex_digit_display_11 (.value({1'b0, cell_5_cmd_2}));  // open: dp

  // Notes on the sheet:
  //   [Hello, world]
  //   Hello, world
  //   contents of rom_1 (hex, n*v repeats v):
  //   10*6 1 3 7*6 3 10*6 3 6 6 6 3 6 4*2 7 0 3 6 6 4 3 6 4 7*6 4 4 6 6 6 4 3 6 6 4 2 2 15*6 4 3 4 6 6 6 4
  //   6*7 4 8*7 4 3 6 4 3 4 8
  //   contents of rom_2 (hex, n*v repeats v):
  //   72*6 4 29*6 4 7*6 4 4 6 6 6 4 79*7 4 55*6 4 24*6 4 6 6 6 4 6*7 4 8*7 4 67*7 4 23*7 4 8
endmodule

// memcell
module \cell  (
  input  IS_TAIL,
  input  IS_HEAD,
  input  IS_ACTIVE_RIGHT,
  input  IS_ACTIVE_LEFT,
  input  [7:0] DATA_IN,
  input  [7:0] DATA_OUT,
  input  [2:0] CMD,
  input  CLK,
  output SET_TAIL,
  output SET_HEAD,
  output IS_ACTIVE,
  output [7:0] DBG_MEM,
  output [2:0] DBG_LED,
  output IS_ACTIVE_2,
  output [7:0] DATA_IN_2,
  output [7:0] DATA_OUT_2,
  output [2:0] CMD_2,
  output CLK_2
);

  wire and_1_out, and_5_out, and_6_out, bitselector_1_out, bitselector_2_out, COUNT, decoder_1_out0, LOAD,
       minus_ACT, not_1_out, not_2_out, not_3_out, not_4_out, not_5_out, plus_1__1, plus_ACT, R_W, RST,
       s_r_ff_1_q, tunnel, WRITE;
  wire [7:0] controlled_buffer_5_out;

  Pull_Resistor #(.pull(1)) pull_resistor_1 (.node(IS_HEAD));
  Pull_Resistor pull_resistor_2 (.node(IS_ACTIVE_LEFT));
  BitSelector #(.width(2)) bitselector_1 (.in({IS_TAIL, IS_HEAD}), .out(bitselector_1_out), .sel(CMD[0]));
  BitSelector #(.width(2)) bitselector_2 (
    .in({IS_ACTIVE_LEFT, IS_ACTIVE_RIGHT}), .out(bitselector_2_out), .sel(CMD[0]));
  and and_1 (and_1_out, plus_1__1, DBG_LED[1]);
  and and_2 (WRITE, R_W, CMD[0], DBG_LED[1]);
  not not_1 (not_1_out, bitselector_1_out);
  not not_2 (not_2_out, DBG_LED[1]);
  assign LOAD = and_1_out ? CMD[0] : 1'bz;  // Controlled_Buffer controlled_buffer_1
  assign COUNT = and_1_out ? 1'b1 : 1'bz;  // Controlled_Buffer controlled_buffer_2
  assign LOAD = WRITE ? 1'b1 : 1'bz;  // Controlled_Buffer controlled_buffer_3
  assign COUNT = WRITE ? 1'b0 : 1'bz;  // Controlled_Buffer controlled_buffer_4
  Pull_Resistor pull_resistor_3 (.node(DATA_IN));
  Pull_Resistor pull_resistor_4 (.node(CMD));
  Pull_Resistor pull_resistor_5 (.node(CLK));
  and and_3 (minus_ACT, DBG_LED[1], tunnel, not_1_out);
  and and_4 (plus_ACT, not_2_out, tunnel, bitselector_2_out);
  Pull_Resistor #(.pull(1)) pull_resistor_6 (.node(IS_TAIL));
  Pull_Resistor pull_resistor_7 (.node(IS_ACTIVE_RIGHT));
  assign controlled_buffer_5_out = WRITE ? DATA_IN : 8'bz;  // Controlled_Buffer controlled_buffer_5
  Pull_Resistor pull_resistor_8 (.node(LOAD));
  Pull_Resistor pull_resistor_9 (.node(COUNT));
  Decoder #(.select(2), .disabled(0), .enable("false")) decoder_1 (
    .out0(decoder_1_out0), .out1(tunnel), .out2(R_W), .out3(plus_1__1), .sel(CMD[2:1]));
  not not_3 (not_3_out, CLK);
  S_R_Flip_Flop s_r_ff_1 (.S(plus_ACT), .clk(CLK), .R(minus_ACT), .Q(s_r_ff_1_q), .reset(RST));  // open: Qn, preset, en
  Counter counter_1 (
    .load(LOAD), .D(controlled_buffer_5_out), .count(COUNT), .Q(DBG_MEM), .clk(CLK), .clr(RST));  // open: carry
  and and_5 (and_5_out, not_4_out, DBG_LED[1], R_W);
  not not_4 (not_4_out, CMD[0]);
  and and_6 (and_6_out, CMD[0], decoder_1_out0);
  D_Flip_Flop d_ff_1 (.clk(not_3_out), .D(s_r_ff_1_q), .Q(DBG_LED[1]), .reset(RST));  // open: Qn, preset, en
  assign DATA_OUT = and_5_out ? DBG_MEM : 8'bz;  // Controlled_Buffer controlled_buffer_6
  D_Flip_Flop d_ff_2 (.clk(CLK), .D(and_6_out), .Q(RST), .reset(not_5_out));  // open: Qn, preset, en
  not not_5 (not_5_out, and_6_out);

  assign CLK_2 = CLK;
  assign CMD_2 = CMD;
  assign DATA_IN_2 = DATA_IN;
  assign DATA_OUT_2 = DATA_OUT;
  assign {DBG_LED[2], DBG_LED[0]} = {IS_TAIL, IS_HEAD};
  assign IS_ACTIVE = DBG_LED[1];
  assign IS_ACTIVE_2 = DBG_LED[1];
  assign SET_HEAD = 1'b0;
  assign SET_TAIL = 1'b0;

  // Other names for the same wires on the sheet: AR = IS_ACTIVE_RIGHT; AL = IS_ACTIVE_LEFT; HEAD = IS_HEAD;
  //   ACT = DBG_LED[1]; TAIL = IS_TAIL; IN[7:0] = DATA_IN; OUT[7:0] = DATA_OUT
endmodule

module tape (
  input  [3:0] DATA,
  input  BF_NEXT,
  input  BF_PREV,
  output [11:0] ADDRESS,
  output [3:0] BF_CMD
);

  wire or_1_out;

  or or_1 (or_1_out, BF_PREV, BF_NEXT);
  Counter #(.width(12), .max('hfff)) counter_1 (
    .load(BF_PREV), .count(or_1_out), .Q(ADDRESS), .clk(or_1_out));  // open: D, carry, clr
  Pull_Resistor pull_resistor_1 (.node(BF_NEXT));
  Pull_Resistor pull_resistor_2 (.node(BF_PREV));

  assign BF_CMD = DATA;

  // Other names for the same wires on the sheet: NEXT = BF_NEXT; PREV = BF_PREV
endmodule

module cpu (
  input  [3:0] CUR_BF,
  input  [7:0] DATA_FROM_CELL,
  input  CLK,
  input  TURN_ON,
  output [6:0] DISP,
  output TTY_CLK,
  output FAKE_ACT,
  output [7:0] DATA_TO_CELL,
  output TAPE_NEXT,
  output TAPE_PREV,
  output [2:0] CMD,
  output CELL_CLK
);

  wire and_1_out, and_2_out, and_3_out, CLEAR_ACT, IS_EXEC, IS_EXECR, IS_EXECW, IS_INIT0, IS_INIT1, IS_INIT2,
       IS_INIT3, IS_INIT4, IS_NEXT, IS_ON, IS_OUT_CMD, IS_RDY, IS_SHOW, IS_SIMPLE_CMD, not_1_out, not_2_out;
  wire [2:0] NEXT_CMD;
  wire [7:0] CUR_STATE, NEXT_STATE;
  wire [7:7] DISP_t;

  D_Flip_Flop d_ff_1 (.Q(IS_ON), .preset(TURN_ON));  // open: clk, D, Qn, en, reset
  and and_1 (and_1_out, IS_INIT0, IS_ON);
  assign NEXT_STATE = IS_EXEC ? 8'h82 : 8'bz;  // Controlled_Buffer controlled_buffer_1
  assign CELL_CLK = IS_EXEC ? CLK : 1'bz;  // Controlled_Buffer controlled_buffer_2
  assign NEXT_STATE = and_1_out ? 8'h1 : 8'bz;  // Controlled_Buffer controlled_buffer_3
  assign NEXT_STATE = IS_INIT3 ? 8'h4 : 8'bz;  // Controlled_Buffer controlled_buffer_4
  assign NEXT_CMD = IS_INIT3 ? 3'b011 : 3'bz;  // Controlled_Buffer controlled_buffer_5
  and and_2 (and_2_out, IS_SIMPLE_CMD, IS_RDY);
  assign NEXT_STATE = and_2_out ? 8'h81 : 8'bz;  // Controlled_Buffer controlled_buffer_6
  D_Flip_Flop d_ff_2 (.Q(FAKE_ACT), .preset(IS_INIT2), .reset(CLEAR_ACT));  // open: clk, D, Qn, en
  Pull_Resistor pull_resistor_1 (.node(CLK));
  assign NEXT_STATE = IS_NEXT ? 8'h80 : 8'bz;  // Controlled_Buffer controlled_buffer_7
  assign TAPE_NEXT = IS_NEXT ? CLK : 1'bz;  // Controlled_Buffer controlled_buffer_8
  Comparator #(.mode("unsigned")) comparator_1 (.a(CUR_STATE), .b({8{1'b0}}), .eq(IS_INIT0));  // open: gt, lt
  Comparator #(.mode("unsigned")) comparator_2 (.a(CUR_STATE), .b(8'h2), .eq(IS_INIT2));  // open: gt, lt
  Comparator #(.mode("unsigned")) comparator_3 (.a(CUR_STATE), .b(8'h4), .eq(IS_INIT4));  // open: gt, lt
  Comparator #(.mode("unsigned")) comparator_4 (.a(CUR_STATE), .b(8'h80), .eq(IS_RDY));  // open: gt, lt
  Comparator #(.mode("unsigned")) comparator_5 (.a(CUR_STATE), .b(8'h82), .eq(IS_NEXT));  // open: gt, lt
  Comparator #(.mode("unsigned")) comparator_6 (.a(CUR_STATE), .b(8'h84), .eq(IS_SHOW));  // open: gt, lt
  assign NEXT_STATE = IS_INIT1 ? 8'h2 : 8'bz;  // Controlled_Buffer controlled_buffer_9
  assign NEXT_CMD = IS_INIT1 ? 3'b001 : 3'bz;  // Controlled_Buffer controlled_buffer_10
  assign NEXT_STATE = IS_INIT4 ? 8'h5 : 8'bz;  // Controlled_Buffer controlled_buffer_11
  assign CELL_CLK = IS_INIT4 ? CLK : 1'bz;  // Controlled_Buffer controlled_buffer_12
  Register STATE (.D(NEXT_STATE), .Q(CUR_STATE), .clk(not_1_out));  // open: en, clr
  not not_1 (not_1_out, CLK);
  and and_3 (and_3_out, IS_OUT_CMD, IS_RDY);
  assign NEXT_STATE = and_3_out ? 8'h83 : 8'bz;  // Controlled_Buffer controlled_buffer_13
  Comparator #(.mode("unsigned")) comparator_7 (.a(CUR_STATE), .b(8'h1), .eq(IS_INIT1));  // open: gt, lt
  Comparator #(.mode("unsigned")) comparator_8 (.a(CUR_STATE), .b(8'h3), .eq(IS_INIT3));  // open: gt, lt
  Comparator #(.mode("unsigned")) comparator_9 (.a(CUR_STATE), .b(8'h5), .eq(CLEAR_ACT));  // open: gt, lt
  Comparator #(.mode("unsigned")) comparator_10 (.a(CUR_STATE), .b(8'h81), .eq(IS_EXEC));  // open: gt, lt
  Comparator #(.mode("unsigned")) comparator_11 (.a(CUR_STATE), .b(8'h83), .eq(IS_EXECW));  // open: gt, lt
  Comparator #(.mode("unsigned")) comparator_12 (.a(CUR_STATE), .b(8'h85), .eq(IS_EXECR));  // open: gt, lt
  assign NEXT_STATE = IS_EXECW ? 8'h84 : 8'bz;  // Controlled_Buffer controlled_buffer_14
  assign CELL_CLK = IS_EXECW ? CLK : 1'bz;  // Controlled_Buffer controlled_buffer_15
  assign NEXT_STATE = IS_INIT2 ? 8'h3 : 8'bz;  // Controlled_Buffer controlled_buffer_16
  assign CELL_CLK = IS_INIT2 ? CLK : 1'bz;  // Controlled_Buffer controlled_buffer_17
  assign NEXT_STATE = CLEAR_ACT ? 8'h80 : 8'bz;  // Controlled_Buffer controlled_buffer_18
  assign NEXT_CMD = CLEAR_ACT ? 3'b000 : 3'bz;  // Controlled_Buffer controlled_buffer_19
  assign NEXT_CMD = IS_RDY ? CUR_BF[2:0] : 3'bz;  // Controlled_Buffer controlled_buffer_20
  Register #(.width(3)) CELL_CMD (.D(NEXT_CMD), .Q(CMD), .clk(not_2_out));  // open: en, clr
  not not_2 (not_2_out, CLK);
  buf buffer_1 (IS_SIMPLE_CMD, CUR_BF[1]);
  Comparator #(.width(3), .mode("unsigned")) comparator_13 (
    .a(CUR_BF[2:0]), .b(3'b100), .eq(IS_OUT_CMD));  // open: gt, lt
  Hex_Digit_Display hex_digit_display_1 (.value({1'b0, CMD}));  // open: dp
  assign NEXT_STATE = IS_SHOW ? 8'h82 : 8'bz;  // Controlled_Buffer controlled_buffer_21
  assign TTY_CLK = IS_SHOW ? CLK : 1'bz;  // Controlled_Buffer controlled_buffer_22
  assign {DISP_t[7], DISP} = IS_SHOW ? DATA_FROM_CELL : 8'bz;  // Controlled_Buffer controlled_buffer_23

  // Other names for the same wires on the sheet: CELL_CMD[2:0] = CMD; CUR_BF_CMD[2:0] = CUR_BF[2:0];
  //   STOP_FLAG = CUR_BF[3]; RESERVED[6:0] = CUR_STATE[6:0]; STATE_INITED = CUR_STATE[7]; DISP_t[6:0] = DISP;
  //   FROM_CELL[7:0] = DATA_FROM_CELL; IS_INIT5 = CLEAR_ACT; SET_ACT = IS_INIT2; TO_CELL[7:0] = DATA_TO_CELL
endmodule
